// Logisim project p0b.circ as structural Verilog: 1 circuit, main circuit main
module main (
  input  din,
  input  clk,
  input  re,
  output hit,
  output [1:0] cou
);

  wire comparator_1_eq, hit_t, multiplexer_4_out;
  wire [1:0] adder_1_out, bit_extender_1_out, D, d1, multiplexer_1_out, multiplexer_2_out, Q;

  Multiplexer #(.width(2)) multiplexer_1 (.in0(D), .in1(2'b00), .out(multiplexer_1_out), .sel(re));  // open: en
  Register #(.width(2)) register_1 (.D(multiplexer_1_out), .Q(Q), .clk(clk));  // open: en, clr
  ROM #(.addrWidth(3), .dataWidth(3)) rom_1 (.addr({Q, din}), .data({hit_t, D}));  // open: sel
  assign bit_extender_1_out = {{1{1'b0}}, hit_t};  // Bit_Extender bit_extender_1
  Adder #(.width(2)) adder_1 (.a(bit_extender_1_out), .b(cou), .out(adder_1_out));  // open: cin, cout
  Comparator #(.width(2), .mode("unsigned")) comparator_1 (.a(cou), .b(2'b11), .eq(comparator_1_eq));  // open: gt, lt
  Multiplexer #(.width(2)) multiplexer_2 (.in0(d1), .in1(2'b00), .out(multiplexer_2_out), .sel(re));  // open: en
  Register #(.width(2)) register_2 (.D(multiplexer_2_out), .Q(cou), .clk(clk));  // open: en, clr
  Multiplexer #(.width(2)) multiplexer_3 (.in0(adder_1_out), .in1(2'b11), .out(d1), .sel(comparator_1_eq));  // open: en
  Multiplexer multiplexer_4 (.in0(hit_t), .in1(1'b0), .out(multiplexer_4_out), .sel(re));  // open: en
  Register #(.width(1)) register_3 (.D(multiplexer_4_out), .Q(hit), .clk(clk));  // open: en, clr

  // Other names for the same wires on the sheet: q1[1:0] = cou

  // Notes on the sheet:
  //   contents of rom_1 (hex, n*v repeats v):
  //   0 1 0 2 3 2 0 5
endmodule
