// Logisim project CRC-8bit.circ as structural Verilog: 2 circuits, main circuit CRC
module CRC (
  input  [7:0] X,
  input  [3:0] B,
  output [10:0] out_3
);

  wire [2:0] n4_bit_1_out_3, n4_bit_2_out_3, n4_bit_3_out_3, n4_bit_4_out_3, n4_bit_5_out_3, n4_bit_7_out_3,
       X_star;

  _4_bit u_4_bit_1 (.X(X[7:4]), .B(B), .out_3(n4_bit_1_out_3));
  _4_bit u_4_bit_2 (.X({X_star, 1'b0}), .B(B), .out_3(n4_bit_2_out_3));
  _4_bit u_4_bit_3 (.X({n4_bit_1_out_3, X[3]}), .B(B), .out_3(n4_bit_3_out_3));
  _4_bit u_4_bit_4 (.X({n4_bit_2_out_3, 1'b0}), .B(B), .out_3(n4_bit_4_out_3));
  _4_bit u_4_bit_5 (.X({n4_bit_3_out_3, X[2]}), .B(B), .out_3(n4_bit_5_out_3));
  // Probe on out_3[2:0]
  _4_bit u_4_bit_6 (.X({n4_bit_4_out_3, 1'b0}), .B(B), .out_3(out_3[2:0]));
  _4_bit u_4_bit_7 (.X({n4_bit_5_out_3, X[1]}), .B(B), .out_3(n4_bit_7_out_3));
  _4_bit u_4_bit_8 (.X({n4_bit_7_out_3, X[0]}), .B(B), .out_3(X_star));

  assign out_3[10:3] = X;
endmodule

module _4_bit (
  input  [3:0] X,
  input  [3:0] B,
  output [2:0] out_3
);

  wire not_1_out;
  wire [3:0] xor_1_out;
  wire [3:3] multiplexer_1_out;

  assign xor_1_out = B ^ X;  // XOR_Gate xor_1, 4 bits wide
  // Probe on {multiplexer_1_out[3], out_3}
  Multiplexer #(.width(4), .enable("false")) multiplexer_1 (
    .in0(xor_1_out), .in1(X), .out({multiplexer_1_out[3], out_3}), .sel(not_1_out));
  not not_1 (not_1_out, X[3]);
endmodule
