// Logisim project Q4.circ as structural Verilog: 1 circuit, main circuit fsm
module fsm (
  input  in_1,
  input  [1:0] in_2,
  output Z
);

  wire and_1_out, and_2_out, clock_1_out, not_1_out, not_2_out, not_3_out, not_4_out, not_5_out, not_6_out,
       Q0, Q1;
  wire [1:0] and_3_out;

  not not_1 (not_1_out, in_2[1]);
  not not_2 (not_2_out, Q1);
  not not_3 (not_3_out, in_2[0]);
  and and_1 (and_1_out, in_2[0], not_1_out);
  and and_2 (and_2_out, not_2_out, not_3_out, Q0);
  not not_4 (not_4_out, in_1);
  and and_3 (and_3_out[0], and_1_out, not_4_out);
  and and_4 (and_3_out[1], not_4_out, and_2_out);
  Clock clock_1 (.out(clock_1_out));
  Register #(.width(2)) register_1 (.D(and_3_out), .en(1'b1), .Q({Q1, Q0}), .clk(clock_1_out), .clr(1'b0));
  not not_5 (not_5_out, Q0);
  not not_6 (not_6_out, in_2[0]);
  and and_5 (Z, not_5_out, Q1, not_6_out);

  // Other names for the same wires on the sheet: CLR = in_1; I0 = in_2[0]; In[1:0] = in_2; I1 = in_2[1]
endmodule
