// Logisim project grf.circ as structural Verilog: 1 circuit, main circuit grf
module grf (
  input  [4:0] in_1,
  input  [4:0] in_2,
  input  in_3,
  input  in_4,
  input  in_5,
  input  [4:0] in_6,
  input  [31:0] WD,
  output [31:0] RD1,
  output [31:0] RD2
);

  wire en0, en1, en2, en3, en4, en5, en6, en7, en8, en9, en10, en11, en12, en13, en14, en15, en16, en17,
       en18, en19, en20, en21, en22, en23, en24, en25, en26, en27, en28, en29, en30, en31;
  wire [31:0] D0, D1, D2, D3, D4, D5, D6, D7, D8, D9, D10, D11, D12, D13, D14, D15, D16, D17, D18, D19, D20,
       D21, D22, D23, D24, D25, D26, D27, D28, D29, D30, D31, R0, R1, R2, R3, R4, R5, R6, R7, R8, R9, R10,
       R11, R12, R13, R14, R15, R16, R17, R18, R19, R20, R21, R22, R23, R24, R25, R26, R27, R28, R29, R30,
       R31;

  Demultiplexer #(.select(5), .width(32), .enable("false")) demultiplexer_1 (
    .out0(D0), .out1(D1), .out2(D2), .out3(D3), .out4(D4), .out5(D5), .out6(D6), .out7(D7), .out8(D8),
    .out9(D9), .out10(D10), .out11(D11), .out12(D12), .out13(D13), .out14(D14), .out15(D15), .out16(D16),
    .out17(D17), .out18(D18), .out19(D19), .out20(D20), .out21(D21), .out22(D22), .out23(D23), .out24(D24),
    .out25(D25), .out26(D26), .out27(D27), .out28(D28), .out29(D29), .out30(D30), .out31(D31), .in(WD),
    .sel(in_6));
  Demultiplexer #(.select(5), .enable("false")) demultiplexer_2 (
    .out0(en0), .out1(en1), .out2(en2), .out3(en3), .out4(en4), .out5(en5), .out6(en6), .out7(en7),
    .out8(en8), .out9(en9), .out10(en10), .out11(en11), .out12(en12), .out13(en13), .out14(en14),
    .out15(en15), .out16(en16), .out17(en17), .out18(en18), .out19(en19), .out20(en20), .out21(en21),
    .out22(en22), .out23(en23), .out24(en24), .out25(en25), .out26(en26), .out27(en27), .out28(en28),
    .out29(en29), .out30(en30), .out31(en31), .in(in_5), .sel(in_6));
  Register #(.width(32)) register_1 (.D(D0), .en(1'b0), .Q(R0), .clk(in_3), .clr(in_4));
  Register #(.width(32)) register_2 (.D(D4), .en(en4), .Q(R4), .clk(in_3), .clr(in_4));
  Register #(.width(32)) register_3 (.D(D8), .en(en8), .Q(R8), .clk(in_3), .clr(in_4));
  Register #(.width(32)) register_4 (.D(D12), .en(en12), .Q(R12), .clk(in_3), .clr(in_4));
  Register #(.width(32)) register_5 (.D(D16), .en(en16), .Q(R16), .clk(in_3), .clr(in_4));
  Register #(.width(32)) register_6 (.D(D20), .en(en20), .Q(R20), .clk(in_3), .clr(in_4));
  Register #(.width(32)) register_7 (.D(D24), .en(en24), .Q(R24), .clk(in_3), .clr(in_4));
  Register #(.width(32)) register_8 (.D(D28), .en(en28), .Q(R28), .clk(in_3), .clr(in_4));
  Register #(.width(32)) register_9 (.D(D1), .en(en1), .Q(R1), .clk(in_3), .clr(in_4));
  Register #(.width(32)) register_10 (.D(D5), .en(en5), .Q(R5), .clk(in_3), .clr(in_4));
  Register #(.width(32)) register_11 (.D(D9), .en(en9), .Q(R9), .clk(in_3), .clr(in_4));
  Register #(.width(32)) register_12 (.D(D13), .en(en13), .Q(R13), .clk(in_3), .clr(in_4));
  Register #(.width(32)) register_13 (.D(D17), .en(en17), .Q(R17), .clk(in_3), .clr(in_4));
  Register #(.width(32)) register_14 (.D(D21), .en(en21), .Q(R21), .clk(in_3), .clr(in_4));
  Register #(.width(32)) register_15 (.D(D25), .en(en25), .Q(R25), .clk(in_3), .clr(in_4));
  Register #(.width(32)) register_16 (.D(D29), .en(en29), .Q(R29), .clk(in_3), .clr(in_4));
  Register #(.width(32)) register_17 (.D(D2), .en(en2), .Q(R2), .clk(in_3), .clr(in_4));
  Register #(.width(32)) register_18 (.D(D6), .en(en6), .Q(R6), .clk(in_3), .clr(in_4));
  Register #(.width(32)) register_19 (.D(D10), .en(en10), .Q(R10), .clk(in_3), .clr(in_4));
  Register #(.width(32)) register_20 (.D(D14), .en(en14), .Q(R14), .clk(in_3), .clr(in_4));
  Register #(.width(32)) register_21 (.D(D18), .en(en18), .Q(R18), .clk(in_3), .clr(in_4));
  Register #(.width(32)) register_22 (.D(D22), .en(en22), .Q(R22), .clk(in_3), .clr(in_4));
  Register #(.width(32)) register_23 (.D(D26), .en(en26), .Q(R26), .clk(in_3), .clr(in_4));
  Register #(.width(32)) register_24 (.D(D30), .en(en30), .Q(R30), .clk(in_3), .clr(in_4));
  Register #(.width(32)) register_25 (.D(D3), .en(en3), .Q(R3), .clk(in_3), .clr(in_4));
  Register #(.width(32)) register_26 (.D(D7), .en(en7), .Q(R7), .clk(in_3), .clr(in_4));
  Register #(.width(32)) register_27 (.D(D11), .en(en11), .Q(R11), .clk(in_3), .clr(in_4));
  Register #(.width(32)) register_28 (.D(D15), .en(en15), .Q(R15), .clk(in_3), .clr(in_4));
  Register #(.width(32)) register_29 (.D(D19), .en(en19), .Q(R19), .clk(in_3), .clr(in_4));
  Register #(.width(32)) register_30 (.D(D23), .en(en23), .Q(R23), .clk(in_3), .clr(in_4));
  Register #(.width(32)) register_31 (.D(D27), .en(en27), .Q(R27), .clk(in_3), .clr(in_4));
  Register #(.width(32)) register_32 (.D(D31), .en(en31), .Q(R31), .clk(in_3), .clr(in_4));
  Multiplexer #(.select(5), .width(32), .enable("false")) multiplexer_1 (
    .in0(R0), .in1(R1), .in2(R2), .in3(R3), .in4(R4), .in5(R5), .in6(R6), .in7(R7), .in8(R8), .in9(R9),
    .in10(R10), .in11(R11), .in12(R12), .in13(R13), .in14(R14), .in15(R15), .in16(R16), .in17(R17),
    .in18(R18), .in19(R19), .in20(R20), .in21(R21), .in22(R22), .in23(R23), .in24(R24), .in25(R25),
    .in26(R26), .in27(R27), .in28(R28), .in29(R29), .in30(R30), .in31(R31), .out(RD1), .sel(in_1));
  Multiplexer #(.select(5), .width(32), .enable("false")) multiplexer_2 (
    .in0(R0), .in1(R1), .in2(R2), .in3(R3), .in4(R4), .in5(R5), .in6(R6), .in7(R7), .in8(R8), .in9(R9),
    .in10(R10), .in11(R11), .in12(R12), .in13(R13), .in14(R14), .in15(R15), .in16(R16), .in17(R17),
    .in18(R18), .in19(R19), .in20(R20), .in21(R21), .in22(R22), .in23(R23), .in24(R24), .in25(R25),
    .in26(R26), .in27(R27), .in28(R28), .in29(R29), .in30(R30), .in31(R31), .out(RD2), .sel(in_2));

  // Other names for the same wires on the sheet: A1[4:0] = in_1; A2[4:0] = in_2; A3[4:0] = in_6; clk = in_3;
  //   re = in_4; WE = in_5
endmodule
