// Logisim project navigation.circ as structural Verilog: 1 circuit, main circuit navigation
module navigation (
  input  [1:0] dir,
  input  clk,
  input  reset,
  output arrive,
  output hit
);

  wire [2:0] POS;
  wire [3:0] rom_1_data;

  ROM #(.addrWidth(5), .dataWidth(4)) rom_1 (.addr({POS, dir}), .data(rom_1_data), .sel(1'b1));
  Register #(.width(4)) register_1 (.D(rom_1_data), .en(1'b1), .Q({hit, POS}), .clk(clk), .clr(reset));
  Comparator #(.width(3)) comparator_1 (.a(POS), .b(3'b100), .eq(arrive));  // open: gt, lt

  // Notes on the sheet:
  //   contents of rom_1 (hex, n*v repeats v):
  //   1 8 8 8 2 3 0 9 a 4 1 a 4 b b 1 0 0 0 0 0 0 0 0 0 0 0 0 0 0 0 0
endmodule
