// Logisim project 1.circ as structural Verilog: 1 circuit, main circuit main
module main (
  input  [7:0] pos_7_0,
  output [5:0] result_5_0
);

  wire _8, EQ, GT, LT, not_1_out, not_2_out;
  wire [3:0] ccw, cw;

  Subtractor #(.width(4)) subtractor_1 (.a(pos_7_0[3:0]), .b(pos_7_0[7:4]), .out(cw), .bin(not_1_out));  // open: bout
  Subtractor #(.width(4)) subtractor_2 (.a(pos_7_0[7:4]), .b(pos_7_0[3:0]), .out(ccw), .bin(not_2_out));  // open: bout
  not not_1 (not_1_out, 1'b1);
  not not_2 (not_2_out, 1'b1);
  and and_1 (_8, cw[3], EQ);
  Multiplexer #(.width(4), .enable("false")) multiplexer_1 (.in0(cw), .in1(ccw), .out(result_5_0[3:0]), .sel(GT));
  Comparator #(.width(4), .mode("unsigned")) comparator_1 (.a(cw), .b(ccw), .gt(GT), .eq(EQ), .lt(LT));
  or or_1 (result_5_0[4], _8, LT);
  or or_2 (result_5_0[5], _8, GT);

  // Other names for the same wires on the sheet: target[3:0] = pos_7_0[3:0]; start[3:0] = pos_7_0[7:4];
  //   dis[3:0] = result_5_0[3:0]
endmodule
