// Logisim project D latch.circ as structural Verilog: 2 circuits, main circuit main
module main (
  input  in_1,
  input  in_2,
  output out_3,
  output out_4
);

  wire d_latch_1_out_3, not_1_out;

  not not_1 (not_1_out, in_2);
  D_Latch d_latch_1 (.in_1(in_1), .in_2(not_1_out), .out_3(d_latch_1_out_3));  // open: out_4
  D_Latch d_latch_2 (.in_1(d_latch_1_out_3), .in_2(in_2), .out_3(out_3), .out_4(out_4));
endmodule

module D_Latch (
  input  in_1,
  input  in_2,
  output out_3,
  output out_4
);

  wire and_1_out, and_2_out, not_1_out, or_1_out, or_2_out;

  not not_1 (not_1_out, in_1);
  and and_1 (and_1_out, in_1, in_2);
  and and_2 (and_2_out, in_2, not_1_out);
  not not_2 (out_3, or_1_out);
  or or_1 (or_1_out, and_1_out, out_4);
  not not_3 (out_4, or_2_out);
  or or_2 (or_2_out, out_3, and_2_out);
endmodule
