// Logisim project mod5.circ as structural Verilog: 2 circuits, main circuit main
module mod5 (
  input  In,
  output S0,
  output S1,
  output S2,
  output S3,
  output S4
);

  wire clock_1_out, nIn, nQ, Q;

  not not_1 (nIn, In);
  Clock clock_1 (.out(clock_1_out));
  D_Flip_Flop d_ff_1 (.clk(clock_1_out), .D(In), .Q(Q), .Qn(nQ));  // open: preset, en, reset
  and and_1 (S1, nQ, nIn);
  and and_2 (S2, nQ, In);
  and and_3 (S3, Q, In);
  and and_4 (S4, Q, nIn);

  assign S0 = 1'b0;

  // Notes on the sheet:
  //   Q = previous bit; next Q = In
  //   mod5 | Mealy FSM | 2^B mod 5
  //   Remainder depends on (Q, In): 00=1, 01=2, 10=4, 11=3
endmodule

module main (
  output In,
  output s0,
  output s1,
  output s2,
  output s3,
  output s4,
  output halt
);

  wire clock_1_out;
  wire [3:0] counter_1_q;

  Clock clock_1 (.out(clock_1_out));
  Counter #(.width(4), .max('he)) counter_1 (
    .Q(counter_1_q), .carry(halt), .clk(clock_1_out));  // open: load, D, count, clr
  ROM #(.addrWidth(4), .dataWidth(1)) rom_1 (.addr(counter_1_q), .data(In));  // open: sel
  mod5 mod5_1 (.In(In), .S0(s0), .S1(s1), .S2(s2), .S3(s3), .S4(s4));

  // Notes on the sheet:
  //   contents of rom_1 (hex, n*v repeats v):
  //   0 1 0 0 1 0 0 1 0 0 1 0 0 1 0 0
endmodule
